# Fritzing sketch esp32_wiring (saved by Fritzing 0.9.3b)
breadboards: 1

parts:
  S1 = Toggle Switch [package=THT]
  U2 = ESP32-38PinWide [part_number=ESP32-38PinWide]
  Capacitive_Soil_Moisture_Sensor1 = DFRobot Capacitive Soil Moisture Sensor V1.0 [part_number=SEN0193]
  Capacitive_Soil_Moisture_Sensor2 = DFRobot Capacitive Soil Moisture Sensor V1.0 [part_number=SEN0193]
  パーツ1 = BME280

nets:
  N1: S1.L1, Capacitive_Soil_Moisture_Sensor1.GND
  VCC: U2.3.3, Capacitive_Soil_Moisture_Sensor1.VCC, Capacitive_Soil_Moisture_Sensor2.VCC, パーツ1.VIN
  N2: U2.GPIO36, Capacitive_Soil_Moisture_Sensor2.A
  N3: U2.GPIO32, Capacitive_Soil_Moisture_Sensor1.A
  GND: U2.GND, Capacitive_Soil_Moisture_Sensor2.GND, パーツ1.GND

custom parts:
  ESP32-38PinWide: Generic 38-Pin ESP32 with wide format (only access to one side of pins on a breadboard) based on Stephen Lilley's HiLetgo ESP-WROOM-32 ESP32 ESP-32S Development Board.
  DFRobot Capacitive Soil Moisture Sensor V1.0: DFRobot Capacitive Soil Moisture Sensor V1.0 This product measures soil moisture levels by capacitive sensing, rather than resistive sensing like other types of moisture sensor. It is made of a corrosion resistant material giving it a long service life. Insert it into soil and impress your friends with the real-time soil moisture data! The product includes an on-board voltage regulator which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
