# Fritzing sketch seismometer (saved by Fritzing 0.9.3b)
breadboards: 1

parts:
  IC2 = IC, DIP package, 14 pins [chip_label=MCP3204]
  IC3 = IC, DIP package, 8 pins [chip_label=KXR94]
  C5 = Ceramic Capacitor [capacitance=0.1µF package="100 mil [THT, multilayer]"]
  C6 = Ceramic Capacitor [capacitance=0.1µF package="100 mil [THT, multilayer]"]
  C7 = Ceramic Capacitor [capacitance=0.1µF package="100 mil [THT, multilayer]"]
  C9 = Ceramic Capacitor [capacitance=1µF package="100 mil [THT, multilayer]"]
  C10 = Electrolytic Capacitor [capacitance=1µF package="100 mil [THT, electrolytic]"]
  D1 = Rectifier Diode [part_number=1N4001 package="300 mil [THT]"]
  IC4 = Voltage Regulator [package=to-92]
  DI1 = 7-Segment LED Display [package=THT]
  R1 = Resistor [tolerance=±5% resistance=330 package="0603 [SMD]"]
  R2 = Resistor [tolerance=±5% resistance=330 package="0603 [SMD]"]
  R3 = Resistor [tolerance=±5% resistance=330 package="0603 [SMD]"]
  R4 = Resistor [tolerance=±5% resistance=330 package="0603 [SMD]"]
  R5 = Resistor [tolerance=±5% resistance=330 package="0603 [SMD]"]
  R6 = Resistor [tolerance=±5% resistance=330 package="0603 [SMD]"]
  R7 = Resistor [tolerance=±5% resistance=330 package="0603 [SMD]"]
  R8 = Resistor [tolerance=±5% resistance=330 package="0603 [SMD]"]
  C11 = Ceramic Capacitor [capacitance=1µF package="100 mil [THT, multilayer]"]
  R9 = Resistor [tolerance=±5% resistance=330 package="0603 [SMD]"]
  LED1 = LED - 3mm [color="Green (555nm)" package="3 mm [THT]"]
  Raspberry_Pi_1 = Raspberry Pi 3 [part_number=RPI-3-V1.2]
  J1 = Piezo Speaker

nets:
  N1: IC2.pin1, IC3.pin6, C7.0
  N2: IC2.pin2, IC3.pin7, C6.0
  N3: IC2.pin3, IC3.pin8, C5.1
  N4: IC2.pin7, IC2.pin12, IC3.pin3, IC3.pin5, C5.0, C6.1, C7.1, C9.1, C10.-, IC4.IN, C11.1, Raspberry_Pi_1.GND
  N5: IC2.pin8, Raspberry_Pi_1.GIPO8
  N6: IC2.pin9, Raspberry_Pi_1.GIPO10
  N7: IC2.pin10, Raspberry_Pi_1.GIPO9
  N8: IC2.pin11, Raspberry_Pi_1.GIPO11
  N9: IC2.pin13, IC2.pin14, IC3.pin1, IC3.pin2, C9.0, C10.+, D1.anode, IC4.GND
  N10: D1.cathode, IC4.OUT, C11.0, Raspberry_Pi_1.5V
  N11: DI1.cathodeE, R3.Pin_1
  N12: DI1.cathodeC, R2.Pin_0
  N13: DI1.cathodeDP, R1.Pin_0
  N14: DI1.cathodeB, R8.Pin_0
  N15: DI1.cathodeA, R7.Pin_0
  N16: DI1.cathodeG, R6.Pin_1
  N17: R1.Pin_1, Raspberry_Pi_1.GIPO12
  N18: R3.Pin_0, Raspberry_Pi_1.GIPO19
  N19: R4.Pin_0, Raspberry_Pi_1.GIPO6
  N20: R5.Pin_0, Raspberry_Pi_1.GIPO17
  N21: R6.Pin_0, Raspberry_Pi_1.GIPO22
  N22: R8.Pin_1, Raspberry_Pi_1.GIPO18
  N23: R9.Pin_0, J1.pin1
  N24: LED1.cathode, Raspberry_Pi_1.GIPO26
  N25: Raspberry_Pi_1.GPIO3, J1.pin2
